// Logisim project solution.circ as structural Verilog: 1 circuit, main circuit mycircuit
module mycircuit (
  input  A,
  input  B,
  input  C,
  output R
);

  wire not_1_out;

  not not_1 (not_1_out, C);
  and and_1 (R, A, not_1_out);
endmodule
