// Logisim project solution.circ as structural Verilog: 1 circuit, main circuit mycircuit
module mycircuit (
  input  A,
  input  B,
  input  C,
  output R
);

  wire not_1_out;

  not not_1 (not_1_out, C);
  xor xor_1 (R, B, not_1_out);
endmodule
