// Logisim project solution.circ as structural Verilog: 1 circuit, main circuit OR3
module OR3 (
  input  A,
  input  B,
  input  C,
  output R
);

  wire transistor_1_out, transistor_2_out;

  Transistor transistor_1 (.in(transistor_2_out), .out(transistor_1_out), .gate(B));
  Transistor transistor_2 (.in(1'b1), .out(transistor_2_out), .gate(C));
  Transistor #(.\type ("n")) transistor_3 (.in(1'b0), .out(R), .gate(A));
  Transistor #(.\type ("n")) transistor_4 (.in(1'b0), .out(R), .gate(B));
  Transistor #(.\type ("n")) transistor_5 (.in(1'b0), .out(R), .gate(C));
  Transistor transistor_6 (.in(transistor_1_out), .out(R), .gate(A));
endmodule
