// Logisim project solution.circ as structural Verilog: 1 circuit, main circuit formula
module formula (
  input  A,
  input  B,
  input  C,
  output R
);

  wire transistor_1_out, transistor_3_out;

  Transistor #(.\type ("n")) transistor_1 (.in(1'b0), .out(transistor_1_out), .gate(B));
  Transistor #(.\type ("n"), .gate("br")) transistor_2 (.in(1'b0), .out(transistor_1_out), .gate(C));
  Transistor #(.\type ("n"), .gate("br")) transistor_3 (.in(1'b0), .out(transistor_3_out), .gate(C));
  Transistor #(.\type ("n")) transistor_4 (.in(transistor_1_out), .out(R), .gate(A));
  Transistor #(.\type ("n"), .gate("br")) transistor_5 (.in(transistor_3_out), .out(R), .gate(B));
  Pull_Resistor #(.pull(1)) pull_resistor_1 (.node(R));
endmodule
