// Logisim project solution.circ as structural Verilog: 1 circuit, main circuit inc
module inc (
  input  [7:0] X,
  output [7:0] R,
  output Cout
);

  wire and_1_out, and_2_out, and_3_out, and_4_out, and_5_out, and_6_out, and_7_out;

  // Probe on X
  xor xor_1 (R[0], 1'b1, X[0]);
  and and_1 (and_1_out, 1'b1, X[0]);
  xor xor_2 (R[1], and_1_out, X[1]);
  xor xor_3 (R[2], and_2_out, X[2]);
  and and_2 (and_2_out, and_1_out, and_1_out, X[1]);
  xor xor_4 (R[3], and_3_out, X[3]);
  xor xor_5 (R[4], and_4_out, X[4]);
  and and_3 (and_3_out, and_2_out, and_2_out, X[2]);
  and and_4 (and_4_out, and_3_out, and_3_out, X[3]);
  xor xor_6 (R[5], and_5_out, X[5]);
  and and_5 (and_5_out, and_4_out, and_4_out, X[4]);
  and and_6 (and_6_out, and_5_out, and_5_out, X[5]);
  xor xor_7 (R[6], and_6_out, X[6]);
  xor xor_8 (R[7], and_7_out, X[7]);
  and and_7 (and_7_out, and_6_out, and_6_out, X[6]);
  and and_8 (Cout, and_7_out, and_7_out, X[7]);
  // Probe on R
endmodule
