// Logisim project solution.circ as structural Verilog: 1 circuit, main circuit inc
module inc (
  input  [7:0] X,
  output [7:0] R,
  output Cout
);

  wire and_1_out, and_2_out, and_3_out, and_4_out, and_5_out, and_6_out, and_7_out, not_1_out, not_2_out,
       not_3_out, not_4_out, not_5_out, not_6_out, not_7_out, not_8_out;

  // Probe on X
  not not_1 (not_1_out, X[1]);
  not not_2 (not_2_out, X[2]);
  not not_3 (not_3_out, X[3]);
  not not_4 (not_4_out, X[4]);
  not not_5 (not_5_out, X[5]);
  not not_6 (not_6_out, X[6]);
  not not_7 (not_7_out, X[7]);
  xor xor_1 (R[0], 1'b1, X[0]);
  and and_1 (and_1_out, 1'b1, not_8_out);
  not not_8 (not_8_out, X[0]);
  xor xor_2 (R[1], and_1_out, X[1]);
  xor xor_3 (R[2], and_2_out, X[2]);
  and and_2 (and_2_out, and_1_out, and_1_out, not_1_out);
  xor xor_4 (R[3], and_3_out, X[3]);
  xor xor_5 (R[4], and_4_out, X[4]);
  and and_3 (and_3_out, and_2_out, and_2_out, not_2_out);
  and and_4 (and_4_out, and_3_out, and_3_out, not_3_out);
  xor xor_6 (R[5], and_5_out, X[5]);
  and and_5 (and_5_out, and_4_out, and_4_out, not_4_out);
  and and_6 (and_6_out, and_5_out, and_5_out, not_5_out);
  xor xor_7 (R[6], and_6_out, X[6]);
  xor xor_8 (R[7], and_7_out, X[7]);
  and and_7 (and_7_out, and_6_out, and_6_out, not_6_out);
  and and_8 (Cout, and_7_out, and_7_out, not_7_out);
  // Probe on R
endmodule
