// Logisim project solution.circ as structural Verilog: 1 circuit, main circuit cmp
module cmp (
  input  [7:0] A,
  input  [7:0] B,
  output Gt,
  output Eq
);


  // Notes on the sheet:
  //   A: pull=up
endmodule
