// Logisim project solution.circ as structural Verilog: 1 circuit, main circuit fib32
module fib32 (
  input  clock,
  output [31:0] a,
  output [5:0] k,
  output stop
);

  wire adder_1_cout, and_1_out, comparator_1_gt, not_1_out;
  wire [31:0] adder_1_out, register_2_q;

  not not_1 (not_1_out, stop);
  Counter #(.width(6), .max('h3f)) counter_1 (.Q(k), .clk(and_1_out));  // open: load, D, count, carry, clr
  and and_1 (and_1_out, clock, not_1_out);
  // Probe on 32'hfffffffe
  // Probe on a
  Register #(.width(32)) register_1 (.D(adder_1_out), .Q(a), .clk(and_1_out));  // open: en, clr
  // Probe on register_2_q
  Register #(.width(32)) register_2 (.D(a), .Q(register_2_q), .clk(and_1_out));  // open: en, clr
  Adder #(.width(32)) adder_1 (.a(register_2_q), .b(a), .out(adder_1_out), .cout(adder_1_cout));  // open: cin
  // Probe on adder_1_out
  Comparator #(.width(32), .mode("unsigned")) comparator_1 (
    .a(adder_1_out), .b(32'hfffffffe), .gt(comparator_1_gt));  // open: eq, lt
  or or_1 (stop, adder_1_cout, comparator_1_gt);
endmodule
