// Logisim project solution.circ as structural Verilog: 2 circuits, main circuit solution
module solution (
  input  [7:0] A,
  input  set,
  input  [7:0] B,
  input  clock,
  output [7:0] GCD,
  output done
);

  wire and_1_out, comparator_1_gt, comparator_1_lt, multiplexer_7_out, not_1_out;
  wire [7:0] demultiplexer_1_out0, demultiplexer_1_out1, multiplexer_1_out, multiplexer_2_out,
       multiplexer_3_out, multiplexer_4_out, multiplexer_5_out, multiplexer_6_out, register_1_q,
       subtractor_1_out;

  // Probe on A
  // Probe on B
  Multiplexer #(.width(8)) multiplexer_1 (
    .in0(multiplexer_3_out), .in1(A), .out(multiplexer_1_out), .sel(set));  // open: en
  Multiplexer #(.width(8)) multiplexer_2 (
    .in0(multiplexer_4_out), .in1(B), .out(multiplexer_2_out), .sel(set));  // open: en
  // Probe on multiplexer_4_out
  // Probe on multiplexer_3_out
  and and_1 (and_1_out, clock, not_1_out);
  Multiplexer #(.width(8)) multiplexer_3 (
    .in0(register_1_q), .in1(demultiplexer_1_out0), .out(multiplexer_3_out), .sel(comparator_1_lt));  // open: en
  not not_1 (not_1_out, multiplexer_7_out);
  // Probe on register_1_q
  Register register_1 (.D(multiplexer_1_out), .Q(register_1_q), .clk(and_1_out));  // open: en, clr
  Multiplexer #(.width(8)) multiplexer_4 (
    .in0(GCD), .in1(demultiplexer_1_out1), .out(multiplexer_4_out), .sel(comparator_1_gt));  // open: en
  // Probe on GCD
  Register register_2 (.D(multiplexer_2_out), .Q(GCD), .clk(and_1_out));  // open: en, clr
  Comparator comparator_1 (.a(GCD), .b(register_1_q), .gt(comparator_1_gt), .eq(done), .lt(comparator_1_lt));
  Demultiplexer #(.width(8)) demultiplexer_1 (
    .out0(demultiplexer_1_out0), .out1(demultiplexer_1_out1), .in(subtractor_1_out), .sel(comparator_1_gt));  // open: en
  Multiplexer #(.width(8)) multiplexer_5 (
    .in0(register_1_q), .in1(GCD), .out(multiplexer_5_out), .sel(comparator_1_gt));  // open: en
  Multiplexer #(.width(8)) multiplexer_6 (
    .in0(register_1_q), .in1(GCD), .out(multiplexer_6_out), .sel(comparator_1_lt));  // open: en
  Subtractor subtractor_1 (.a(multiplexer_5_out), .b(multiplexer_6_out), .out(subtractor_1_out));  // open: bin, bout
  // Probe on subtractor_1_out
  Multiplexer multiplexer_7 (.in0(done), .in1(1'b0), .out(multiplexer_7_out), .sel(set));  // open: en
  // Probe on GCD
endmodule

module stopper (
  input  run_prime,
  input  stop,
  input  clock_in,
  output clock_out
);

  wire multiplexer_1_out, not_1_out, or_1_out, register_1_q;

  not not_1 (not_1_out, stop);
  Multiplexer #(.enable("false")) multiplexer_1 (
    .in0(not_1_out), .in1(run_prime), .out(multiplexer_1_out), .sel(run_prime));
  or or_1 (or_1_out, run_prime, register_1_q);
  Register #(.width(1), .trigger("falling")) register_1 (
    .D(multiplexer_1_out), .en(or_1_out), .Q(register_1_q), .clk(clock_in));  // open: clr
  and and_1 (clock_out, register_1_q, clock_in);
endmodule
