// Logisim project solution.circ as structural Verilog: 3 circuits, main circuit hotel.safe
module hotel_safe (
  input  [3:0] Pad,
  input  clock,
  input  D_open,
  output [15:0] Disp,
  output D_locked
);

  wire _0_out, _1_out, _2_out, _3_out, _4_out, _5_out, _6_out, _7_out, _8_out, _9_out, butdrv_1_gnd,
       butdrv_2_gnd, butdrv_3_gnd, butdrv_4_gnd, butdrv_5_gnd, butdrv_6_gnd, butdrv_7_gnd, butdrv_8_gnd,
       butdrv_9_gnd, butdrv_10_gnd, butdrv_11_gnd, butdrv_12_gnd, button_out, R_out;
  wire [3:0] button, not_1_out;

  butdrv butdrv_1 (
    .b1(butdrv_1_gnd), .b2(butdrv_1_gnd), .b3(butdrv_1_gnd), .gnd(butdrv_1_gnd), .but(_1_out),
    .out_7({clock, Pad}));  // open: b0
  Button _1 (.out(_1_out));
  Button _4 (.out(_4_out));
  butdrv butdrv_2 (
    .b0(butdrv_2_gnd), .b1(butdrv_2_gnd), .b3(butdrv_2_gnd), .gnd(butdrv_2_gnd), .but(_4_out),
    .out_7({clock, Pad}));  // open: b2
  Button _7 (.out(_7_out));
  butdrv butdrv_3 (.b3(butdrv_3_gnd), .gnd(butdrv_3_gnd), .but(_7_out), .out_7({clock, Pad}));  // open: b0, b1, b2
  butdrv butdrv_4 (
    .b0(butdrv_4_gnd), .b2(butdrv_4_gnd), .gnd(butdrv_4_gnd), .but(button_out), .out_7({clock, Pad}));  // open: b1, b3
  Button u_button (.out(button_out));
  Pull_Resistor pull_resistor_1 (.node(clock));
  butdrv butdrv_5 (
    .b2(butdrv_5_gnd), .b3(butdrv_5_gnd), .gnd(butdrv_5_gnd), .but(_3_out), .out_7({clock, Pad}));  // open: b0, b1
  Button _2 (.out(_2_out));
  Button _3 (.out(_3_out));
  butdrv butdrv_6 (
    .b0(butdrv_6_gnd), .b2(butdrv_6_gnd), .b3(butdrv_6_gnd), .gnd(butdrv_6_gnd), .but(_2_out),
    .out_7({clock, Pad}));  // open: b1
  butdrv butdrv_7 (
    .b0(butdrv_7_gnd), .b3(butdrv_7_gnd), .gnd(butdrv_7_gnd), .but(_6_out), .out_7({clock, Pad}));  // open: b1, b2
  butdrv butdrv_8 (
    .b1(butdrv_8_gnd), .b3(butdrv_8_gnd), .gnd(butdrv_8_gnd), .but(_5_out), .out_7({clock, Pad}));  // open: b0, b2
  Button _5 (.out(_5_out));
  Button _6 (.out(_6_out));
  Button _9 (.out(_9_out));
  butdrv butdrv_9 (
    .b0(butdrv_9_gnd), .b1(butdrv_9_gnd), .b2(butdrv_9_gnd), .gnd(butdrv_9_gnd), .but(_8_out),
    .out_7({clock, Pad}));  // open: b3
  Button _8 (.out(_8_out));
  butdrv butdrv_10 (
    .b1(butdrv_10_gnd), .b2(butdrv_10_gnd), .gnd(butdrv_10_gnd), .but(_9_out), .out_7({clock, Pad}));  // open: b0, b3
  Button R (.out(R_out));
  Button _0 (.out(_0_out));
  butdrv butdrv_11 (.b2(butdrv_11_gnd), .gnd(butdrv_11_gnd), .but(R_out), .out_7({clock, Pad}));  // open: b0, b1, b3
  butdrv butdrv_12 (
    .b0(butdrv_12_gnd), .b1(butdrv_12_gnd), .b2(butdrv_12_gnd), .b3(butdrv_12_gnd), .gnd(butdrv_12_gnd),
    .but(_0_out), .out_7({clock, Pad}));
  Pull_Resistor pull_resistor_2 (.node(Pad[2]));
  Pull_Resistor pull_resistor_3 (.node(Pad[1]));
  Pull_Resistor pull_resistor_4 (.node(Pad[0]));
  Hex_Digit_Display hex_digit_display_1 (.value(Disp[15:12]));  // open: dp
  Pull_Resistor pull_resistor_5 (.node(Pad[3]));
  assign not_1_out = ~Pad;  // NOT_Gate not_1, 4 bits wide
  Hex_Digit_Display hex_digit_display_2 (.value(Disp[11:8]));  // open: dp
  Hex_Digit_Display hex_digit_display_3 (.value(Disp[7:4]));  // open: dp
  assign button = ~not_1_out;  // NOT_Gate not_2, 4 bits wide
  LED led_1 (.in(D_locked));
  Hex_Digit_Display hex_digit_display_4 (.value(Disp[3:0]));  // open: dp
  assign D_open = D_locked ? ~D_locked : 1'bz;  // Controlled_Inverter controlled_inverter_1
  Pull_Resistor pull_resistor_6 (.node(D_locked));

  // Other names for the same wires on the sheet: clk = clock; D2[3:0] = Disp[11:8]; D3[3:0] = Disp[15:12];
  //   D0[3:0] = Disp[3:0]; D1[3:0] = Disp[7:4]; locked = D_locked; open = D_open

  // Notes on the sheet:
  //   to robot tester
  //   HOTEL ROOM SAFE
  //   LOCKED
  //   to robot tester
endmodule

module butdrv (
  input  b0,
  input  b1,
  input  b2,
  input  b3,
  input  but,
  output gnd,
  output [4:0] out_7
);

  Pull_Resistor #(.pull(1)) pull_resistor_1 (.node(b0));
  Pull_Resistor #(.pull(1)) pull_resistor_2 (.node(b3));
  Pull_Resistor #(.pull(1)) pull_resistor_3 (.node(b1));
  Pull_Resistor #(.pull(1)) pull_resistor_4 (.node(b2));
  assign out_7 = but ? {but, b3, b2, b1, b0} : 5'bz;  // Controlled_Buffer controlled_buffer_1

  assign gnd = 1'b0;
endmodule

module RS_flip_flop (
  input  S,
  input  R,
  output Q,
  output Q_prime
);

  S_R_Flip_Flop #(.trigger("low")) s_r_ff_1 (.S(S), .clk(1'b0), .R(R), .Q(Q), .Qn(Q_prime));  // open: preset, reset, en
endmodule
